// Logisim project basic gates.circ as structural Verilog: 1 circuit, main circuit main
module main (
  input  in_1,
  input  in_2,
  input  in_3,
  input  in_4,
  input  in_5,
  input  in_6,
  input  in_7,
  input  in_8,
  input  in_9,
  input  in_10,
  input  in_11,
  input  in_12,
  input  in_13
);

  wire and_1_out, nand_1_out, nor_1_out, not_1_out, or_1_out, xnor_1_out, xor_1_out;

  not not_1 (not_1_out, in_1);
  LED led_1 (.in(not_1_out));
  LED led_2 (.in(and_1_out));
  and and_1 (and_1_out, in_2, in_3);
  LED led_3 (.in(or_1_out));
  or or_1 (or_1_out, in_4, in_5);
  LED led_4 (.in(nor_1_out));
  nor nor_1 (nor_1_out, in_6, in_7);
  nand nand_1 (nand_1_out, in_8, in_9);
  LED led_5 (.in(nand_1_out));
  xor xor_1 (xor_1_out, in_10, in_11);
  xnor xnor_1 (xnor_1_out, in_12, in_13);
  LED led_6 (.in(xor_1_out));
  LED led_7 (.in(xnor_1_out));

  // Notes on the sheet:
  //   NOT gate
  //   AND gate
  //   OR gate
  //   NOR gate
  //   NAND gate
  //   XOR gate
  //   XNOR gate
endmodule
