// Logisim project demultiplexer 4 is to 1.circ as structural Verilog: 1 circuit, main circuit main
module main (
  input  in_1,
  input  in_2,
  input  in_3,
  input  in_4,
  input  in_5,
  input  [1:0] in_6,
  input  in_7,
  input  in_8,
  input  in_9,
  input  in_10,
  input  in_11,
  input  in_12,
  input  D3
);

  wire and_1_out, and_2_out, and_3_out, and_4_out, demultiplexer_1_out0, demultiplexer_1_out1,
       demultiplexer_1_out2, demultiplexer_1_out3, not_1_out, not_2_out, undriven;

  not not_1 (not_1_out, in_7);
  not not_2 (not_2_out, in_8);
  and and_1 (and_1_out, in_8, in_10, not_1_out, not_2_out);
  and and_2 (and_2_out, in_8, in_11, in_7, not_2_out);
  and and_3 (and_3_out, in_8, in_12, not_1_out, in_8);
  and and_4 (and_4_out, in_8, D3, in_7, in_8);
  LED led_1 ();  // open: in
  LED led_2 (.in(and_1_out));
  LED led_3 (.in(and_2_out));
  LED led_4 (.in(and_3_out));
  LED led_5 (.in(and_4_out));
  Demultiplexer #(.select(2)) demultiplexer_1 (
    .out0(demultiplexer_1_out0), .out1(demultiplexer_1_out1), .out2(demultiplexer_1_out2),
    .out3(demultiplexer_1_out3), .in(undriven), .sel(in_6), .en(in_5));

  // Notes on the sheet:
  //   Demultiplexer 4:1
  //   D0
  //   D1
  //   D2
  //   S0
  //   so-
  //   S1
  //   S1-
  //   E
endmodule
