// Logisim project multiplexer 4 is to 1.circ as structural Verilog: 1 circuit, main circuit main
module main (
  input  in_1,
  input  in_2,
  input  in_3,
  input  in_4,
  input  in_5,
  input  in_6,
  input  in_7,
  input  in_8,
  input  [1:0] in_9,
  input  in_10,
  input  in_11,
  input  in_12,
  input  D3
);

  wire and_1_out, and_2_out, and_3_out, and_4_out, multiplexer_1_out, not_1_out, not_2_out, or_1_out;

  not not_1 (not_1_out, in_5);
  not not_2 (not_2_out, in_6);
  and and_1 (and_1_out, in_6, in_10, not_1_out, not_2_out);
  and and_2 (and_2_out, in_6, in_11, in_5, not_2_out);
  and and_3 (and_3_out, in_6, in_12, not_1_out, in_6);
  and and_4 (and_4_out, in_6, D3, in_5, in_6);
  or or_1 (or_1_out, and_1_out, and_2_out, and_3_out, and_4_out);
  Multiplexer #(.select(2)) multiplexer_1 (
    .in0(in_1), .in1(in_2), .in2(in_3), .in3(in_4), .out(multiplexer_1_out), .sel(in_9), .en(in_8));
  LED led_1 (.in(multiplexer_1_out));
  LED led_2 (.in(or_1_out));

  // Notes on the sheet:
  //   D0
  //   D1
  //   D2
  //   Multiplexer 4:1
  //   S0
  //   so-
  //   S1
  //   S1-
  //   E
endmodule
